# Fritzing sketch R02_N1 (saved by Fritzing 0.9.6b)
breadboards: 1

parts:
  Componente1 = Arduino Uno (Rev3)
  J2 = Piezo Speaker
  LED2 = smd LED [color="Red (633nm)" package="0603 [SMD]"]
  Mod3 = MQ-7 breakout
  R2 = Resistor [tolerance=±5% resistance=220 package="2010 [SMD]"]  # not connected

nets:
  N1: Componente1.A0, Mod3.AO
  N2: Componente1.D6_PWM, LED2.cathode
  N3: Componente1.D7, J2.pin2
  GND: Componente1.GND, Mod3.GND

custom parts:
  MQ-7 breakout: MQ-5 gas sensor
