# Fritzing sketch R02_N2 (saved by Fritzing 0.9.6b)
breadboards: 1

parts:
  Componente1 = Arduino Uno (Rev3)
  LCM1602_IIC2 = LCM1602 IIC [part_number="LCM1602 IIC" chip_label="LCM1602 IIC" package="DIP (Dual Inline) [THT]"]
  LCD2 = LCD screen
  J2 = Piezo Speaker
  LED2 = smd LED [color="Red (633nm)" package="0603 [SMD]"]
  Mod3 = MQ-7 breakout
  R2 = Resistor [tolerance=±5% resistance=220 package="2010 [SMD]"]  # not connected

nets:
  N1: Componente1.A0, Mod3.AO
  N2: Componente1.A4/SDA, LCM1602_IIC2.SDA
  N3: Componente1.A5/SCL, LCM1602_IIC2.SCL
  N4: Componente1.D6_PWM, LED2.cathode
  N5: Componente1.D7, J2.pin2
  5V: Componente1.5V, LCM1602_IIC2.VCC
  GND: Componente1.GND, LCM1602_IIC2.GND, Mod3.GND
  VSS: LCM1602_IIC2.VSS, LCD2.VSS
  VDD: LCM1602_IIC2.VDD, LCD2.VDD
  N6: LCM1602_IIC2.V0, LCD2.V0
  N7: LCM1602_IIC2.RS, LCD2.RS
  N8: LCM1602_IIC2.RW, LCD2.R/W
  N9: LCM1602_IIC2.E, LCD2.E
  N10: LCM1602_IIC2.D0, LCD2.DB0
  N11: LCM1602_IIC2.D1, LCD2.DB1
  N12: LCM1602_IIC2.D2, LCD2.DB2
  N13: LCM1602_IIC2.D3, LCD2.DB3
  N14: LCM1602_IIC2.D4, LCD2.DB4
  N15: LCM1602_IIC2.D5, LCD2.DB5
  N16: LCM1602_IIC2.D6, LCD2.DB6
  N17: LCM1602_IIC2.D7, LCD2.DB7
  N18: LCM1602_IIC2.A, LCD2.LED+
  N19: LCM1602_IIC2.K, LCD2.LED-
  N20: LCM1602_IIC2.LED_A, LCM1602_IIC2.LED_B

custom parts:
  LCM1602 IIC: I2C-Module to use a 1602 or 2004 LCD on with the wire.h libory Serial LCD Modul
  MQ-7 breakout: MQ-5 gas sensor
